// Logisim project snake.circ as structural Verilog: 7 circuits, main circuit main
module main (
);

  wire contr_1_out_7, desno, dole, gore, levo;
  wire [4:0] contr_1_out_5, contr_1_out_6;
  wire [31:0] kont_izlaz_1_out_4, kont_izlaz_1_out_5, kont_izlaz_1_out_6, kont_izlaz_1_out_7,
       kont_izlaz_1_out_8, kont_izlaz_1_out_9, kont_izlaz_1_out_10, kont_izlaz_1_out_11, kont_izlaz_1_out_12,
       kont_izlaz_1_out_13, kont_izlaz_1_out_14, kont_izlaz_1_out_15, kont_izlaz_1_out_16,
       kont_izlaz_1_out_17, kont_izlaz_1_out_18, kont_izlaz_1_out_19, kont_izlaz_1_out_20,
       kont_izlaz_1_out_21, kont_izlaz_1_out_22, kont_izlaz_1_out_23, kont_izlaz_1_out_24,
       kont_izlaz_1_out_25, kont_izlaz_1_out_26, kont_izlaz_1_out_27, kont_izlaz_1_out_28,
       kont_izlaz_1_out_29, kont_izlaz_1_out_30, kont_izlaz_1_out_31, kont_izlaz_1_out_32,
       kont_izlaz_1_out_33, kont_izlaz_1_out_34, kont_izlaz_1_out_35;

  DotMatrix #(.inputtype("row"), .matrixcols(32), .matrixrows(32)) dotmatrix_1 (
    .row0(kont_izlaz_1_out_4), .row1(kont_izlaz_1_out_5), .row2(kont_izlaz_1_out_6),
    .row3(kont_izlaz_1_out_7), .row4(kont_izlaz_1_out_8), .row5(kont_izlaz_1_out_9),
    .row6(kont_izlaz_1_out_10), .row7(kont_izlaz_1_out_11), .row8(kont_izlaz_1_out_12),
    .row9(kont_izlaz_1_out_13), .row10(kont_izlaz_1_out_14), .row11(kont_izlaz_1_out_15),
    .row12(kont_izlaz_1_out_16), .row13(kont_izlaz_1_out_17), .row14(kont_izlaz_1_out_18),
    .row15(kont_izlaz_1_out_19), .row16(kont_izlaz_1_out_20), .row17(kont_izlaz_1_out_21),
    .row18(kont_izlaz_1_out_22), .row19(kont_izlaz_1_out_23), .row20(kont_izlaz_1_out_24),
    .row21(kont_izlaz_1_out_25), .row22(kont_izlaz_1_out_26), .row23(kont_izlaz_1_out_27),
    .row24(kont_izlaz_1_out_28), .row25(kont_izlaz_1_out_29), .row26(kont_izlaz_1_out_30),
    .row27(kont_izlaz_1_out_31), .row28(kont_izlaz_1_out_32), .row29(kont_izlaz_1_out_33),
    .row30(kont_izlaz_1_out_34), .row31(kont_izlaz_1_out_35));
  KONT_IZLAZ kont_izlaz_1 (
    .in_1(contr_1_out_5), .in_2(contr_1_out_6), .CLOCK(contr_1_out_7), .out_4(kont_izlaz_1_out_4),
    .out_5(kont_izlaz_1_out_5), .out_6(kont_izlaz_1_out_6), .out_7(kont_izlaz_1_out_7),
    .out_8(kont_izlaz_1_out_8), .out_9(kont_izlaz_1_out_9), .out_10(kont_izlaz_1_out_10),
    .out_11(kont_izlaz_1_out_11), .out_12(kont_izlaz_1_out_12), .out_13(kont_izlaz_1_out_13),
    .out_14(kont_izlaz_1_out_14), .out_15(kont_izlaz_1_out_15), .out_16(kont_izlaz_1_out_16),
    .out_17(kont_izlaz_1_out_17), .out_18(kont_izlaz_1_out_18), .out_19(kont_izlaz_1_out_19),
    .out_20(kont_izlaz_1_out_20), .out_21(kont_izlaz_1_out_21), .out_22(kont_izlaz_1_out_22),
    .out_23(kont_izlaz_1_out_23), .out_24(kont_izlaz_1_out_24), .out_25(kont_izlaz_1_out_25),
    .out_26(kont_izlaz_1_out_26), .out_27(kont_izlaz_1_out_27), .out_28(kont_izlaz_1_out_28),
    .out_29(kont_izlaz_1_out_29), .out_30(kont_izlaz_1_out_30), .out_31(kont_izlaz_1_out_31),
    .out_32(kont_izlaz_1_out_32), .out_33(kont_izlaz_1_out_33), .out_34(kont_izlaz_1_out_34),
    .out_35(kont_izlaz_1_out_35));
  CONTR contr_1 (
    .out_5(contr_1_out_5), .out_6(contr_1_out_6), .out_7(contr_1_out_7), .in_1(desno), .in_2(levo),
    .in_3(gore), .in_4(dole));
  Button button (.out(gore));
  Button button_2 (.out(levo));
  Button v (.out(dole));
  Button button_3 (.out(desno));
endmodule

module KONT_IZLAZ (
  input  [4:0] in_1,
  input  [4:0] in_2,
  input  CLOCK,
  output [31:0] out_4,
  output [31:0] out_5,
  output [31:0] out_6,
  output [31:0] out_7,
  output [31:0] out_8,
  output [31:0] out_9,
  output [31:0] out_10,
  output [31:0] out_11,
  output [31:0] out_12,
  output [31:0] out_13,
  output [31:0] out_14,
  output [31:0] out_15,
  output [31:0] out_16,
  output [31:0] out_17,
  output [31:0] out_18,
  output [31:0] out_19,
  output [31:0] out_20,
  output [31:0] out_21,
  output [31:0] out_22,
  output [31:0] out_23,
  output [31:0] out_24,
  output [31:0] out_25,
  output [31:0] out_26,
  output [31:0] out_27,
  output [31:0] out_28,
  output [31:0] out_29,
  output [31:0] out_30,
  output [31:0] out_31,
  output [31:0] out_32,
  output [31:0] out_33,
  output [31:0] out_34,
  output [31:0] out_35
);

  wire clock_1_out, kont_mem_1_enable, SET_CL;
  wire [4:0] KMX, KMY;

  Clock clock_1 (.out(clock_1_out));
  KONT_MEM kont_mem_1 (
    .in_1(in_1), .in_2(in_2), .CLK(CLOCK), .X(KMX), .Y(KMY), .SET_CL(SET_CL), .Enable(kont_mem_1_enable),
    .in_4(clock_1_out));
  REG1028_LD reg1028_ld_1 (
    .X(KMX), .in_2(KMY), .SET_CLEAR(SET_CL), .out_6(out_4), .out_7(out_5), .out_8(out_6), .out_9(out_7),
    .out_10(out_8), .out_11(out_9), .out_12(out_10), .out_13(out_11), .out_14(out_12), .out_15(out_13),
    .out_16(out_14), .out_17(out_15), .out_18(out_16), .out_19(out_17), .out_20(out_18), .out_21(out_19),
    .out_22(out_20), .out_23(out_21), .out_24(out_22), .out_25(out_23), .out_26(out_24), .out_27(out_25),
    .out_28(out_26), .out_29(out_27), .out_30(out_28), .out_31(out_29), .out_32(out_30), .out_33(out_31),
    .out_34(out_32), .out_35(out_33), .out_36(out_34), .out_37(out_35), .ENABLE(kont_mem_1_enable),
    .CLOCK(clock_1_out));
  DotMatrix #(.inputtype("row"), .matrixcols(32), .matrixrows(32)) dotmatrix_1 (
    .row0(out_4), .row1(out_5), .row2(out_6), .row3(out_7), .row4(out_8), .row5(out_9), .row6(out_10),
    .row7(out_11), .row8(out_12), .row9(out_13), .row10(out_14), .row11(out_15), .row12(out_16),
    .row13(out_17), .row14(out_18), .row15(out_19), .row16(out_20), .row17(out_21), .row18(out_22),
    .row19(out_23), .row20(out_24), .row21(out_25), .row22(out_26), .row23(out_27), .row24(out_28),
    .row25(out_29), .row26(out_30), .row27(out_31), .row28(out_32), .row29(out_33), .row30(out_34),
    .row31(out_35));

  // Other names for the same wires on the sheet: CLK = CLOCK
endmodule

module REG1028_LD (
  input  [4:0] X,
  input  [4:0] in_2,
  input  SET_CLEAR,
  input  ENABLE,
  input  CLOCK,
  output [31:0] out_6,
  output [31:0] out_7,
  output [31:0] out_8,
  output [31:0] out_9,
  output [31:0] out_10,
  output [31:0] out_11,
  output [31:0] out_12,
  output [31:0] out_13,
  output [31:0] out_14,
  output [31:0] out_15,
  output [31:0] out_16,
  output [31:0] out_17,
  output [31:0] out_18,
  output [31:0] out_19,
  output [31:0] out_20,
  output [31:0] out_21,
  output [31:0] out_22,
  output [31:0] out_23,
  output [31:0] out_24,
  output [31:0] out_25,
  output [31:0] out_26,
  output [31:0] out_27,
  output [31:0] out_28,
  output [31:0] out_29,
  output [31:0] out_30,
  output [31:0] out_31,
  output [31:0] out_32,
  output [31:0] out_33,
  output [31:0] out_34,
  output [31:0] out_35,
  output [31:0] out_36,
  output [31:0] out_37
);

  wire I0, I1, I2, I3, I4, I5, I6, I7, I8, I9, I10, I11, I12, I13, I14, I15, I16, I17, I18, I19, I20, I21,
       I22, I23, I24, I25, I26, I27, I28, I29, I30, I31;
  wire [31:0] and_1_out, controlled_buffer_1_out, LD, multiplexer_1_out, not_1_out, or_1_out, Y;

  Decoder #(.select(5)) decoder_1 (
    .out0(I0), .out1(I1), .out2(I2), .out3(I3), .out4(I4), .out5(I5), .out6(I6), .out7(I7), .out8(I8),
    .out9(I9), .out10(I10), .out11(I11), .out12(I12), .out13(I13), .out14(I14), .out15(I15), .out16(I16),
    .out17(I17), .out18(I18), .out19(I19), .out20(I20), .out21(I21), .out22(I22), .out23(I23), .out24(I24),
    .out25(I25), .out26(I26), .out27(I27), .out28(I28), .out29(I29), .out30(I30), .out31(I31), .sel(X));  // open: en
  assign controlled_buffer_1_out = I0 ? out_6 : 32'bz;  // Controlled_Buffer controlled_buffer_1
  assign controlled_buffer_1_out = I1 ? out_7 : 32'bz;  // Controlled_Buffer controlled_buffer_2
  assign controlled_buffer_1_out = I2 ? out_8 : 32'bz;  // Controlled_Buffer controlled_buffer_3
  assign controlled_buffer_1_out = I3 ? out_9 : 32'bz;  // Controlled_Buffer controlled_buffer_4
  assign controlled_buffer_1_out = I4 ? out_10 : 32'bz;  // Controlled_Buffer controlled_buffer_5
  assign controlled_buffer_1_out = I5 ? out_11 : 32'bz;  // Controlled_Buffer controlled_buffer_6
  assign controlled_buffer_1_out = I6 ? out_12 : 32'bz;  // Controlled_Buffer controlled_buffer_7
  assign controlled_buffer_1_out = I7 ? out_13 : 32'bz;  // Controlled_Buffer controlled_buffer_8
  REG32_LD reg32_ld_1 (.in_1(LD), .LD(I0), .out_4(out_6), .in_3(CLOCK));
  REG32_LD reg32_ld_2 (.in_1(LD), .LD(I1), .out_4(out_7), .in_3(CLOCK));
  REG32_LD reg32_ld_3 (.in_1(LD), .LD(I2), .out_4(out_8), .in_3(CLOCK));
  REG32_LD reg32_ld_4 (.in_1(LD), .LD(I3), .out_4(out_9), .in_3(CLOCK));
  REG32_LD reg32_ld_5 (.in_1(LD), .LD(I4), .out_4(out_10), .in_3(CLOCK));
  REG32_LD reg32_ld_6 (.in_1(LD), .LD(I5), .out_4(out_11), .in_3(CLOCK));
  REG32_LD reg32_ld_7 (.in_1(LD), .LD(I6), .out_4(out_12), .in_3(CLOCK));
  REG32_LD reg32_ld_8 (.in_1(LD), .LD(I7), .out_4(out_13), .in_3(CLOCK));
  assign controlled_buffer_1_out = I8 ? out_14 : 32'bz;  // Controlled_Buffer controlled_buffer_9
  assign controlled_buffer_1_out = I9 ? out_15 : 32'bz;  // Controlled_Buffer controlled_buffer_10
  assign controlled_buffer_1_out = I10 ? out_16 : 32'bz;  // Controlled_Buffer controlled_buffer_11
  assign controlled_buffer_1_out = I11 ? out_17 : 32'bz;  // Controlled_Buffer controlled_buffer_12
  assign controlled_buffer_1_out = I12 ? out_18 : 32'bz;  // Controlled_Buffer controlled_buffer_13
  assign controlled_buffer_1_out = I13 ? out_19 : 32'bz;  // Controlled_Buffer controlled_buffer_14
  assign controlled_buffer_1_out = I14 ? out_20 : 32'bz;  // Controlled_Buffer controlled_buffer_15
  assign controlled_buffer_1_out = I15 ? out_21 : 32'bz;  // Controlled_Buffer controlled_buffer_16
  assign controlled_buffer_1_out = I16 ? out_22 : 32'bz;  // Controlled_Buffer controlled_buffer_17
  assign controlled_buffer_1_out = I17 ? out_23 : 32'bz;  // Controlled_Buffer controlled_buffer_18
  assign controlled_buffer_1_out = I18 ? out_24 : 32'bz;  // Controlled_Buffer controlled_buffer_19
  assign controlled_buffer_1_out = I19 ? out_25 : 32'bz;  // Controlled_Buffer controlled_buffer_20
  assign controlled_buffer_1_out = I20 ? out_26 : 32'bz;  // Controlled_Buffer controlled_buffer_21
  assign controlled_buffer_1_out = I21 ? out_27 : 32'bz;  // Controlled_Buffer controlled_buffer_22
  assign controlled_buffer_1_out = I22 ? out_28 : 32'bz;  // Controlled_Buffer controlled_buffer_23
  assign controlled_buffer_1_out = I23 ? out_29 : 32'bz;  // Controlled_Buffer controlled_buffer_24
  REG32_LD reg32_ld_9 (.in_1(LD), .LD(I8), .out_4(out_14), .in_3(CLOCK));
  REG32_LD reg32_ld_10 (.in_1(LD), .LD(I9), .out_4(out_15), .in_3(CLOCK));
  REG32_LD reg32_ld_11 (.in_1(LD), .LD(I10), .out_4(out_16), .in_3(CLOCK));
  REG32_LD reg32_ld_12 (.in_1(LD), .LD(I11), .out_4(out_17), .in_3(CLOCK));
  REG32_LD reg32_ld_13 (.in_1(LD), .LD(I12), .out_4(out_18), .in_3(CLOCK));
  REG32_LD reg32_ld_14 (.in_1(LD), .LD(I13), .out_4(out_19), .in_3(CLOCK));
  REG32_LD reg32_ld_15 (.in_1(LD), .LD(I14), .out_4(out_20), .in_3(CLOCK));
  REG32_LD reg32_ld_16 (.in_1(LD), .LD(I15), .out_4(out_21), .in_3(CLOCK));
  assign controlled_buffer_1_out = I24 ? out_30 : 32'bz;  // Controlled_Buffer controlled_buffer_25
  assign controlled_buffer_1_out = I25 ? out_31 : 32'bz;  // Controlled_Buffer controlled_buffer_26
  assign controlled_buffer_1_out = I26 ? out_32 : 32'bz;  // Controlled_Buffer controlled_buffer_27
  assign controlled_buffer_1_out = I27 ? out_33 : 32'bz;  // Controlled_Buffer controlled_buffer_28
  assign controlled_buffer_1_out = I28 ? out_34 : 32'bz;  // Controlled_Buffer controlled_buffer_29
  assign controlled_buffer_1_out = I29 ? out_35 : 32'bz;  // Controlled_Buffer controlled_buffer_30
  assign controlled_buffer_1_out = I30 ? out_36 : 32'bz;  // Controlled_Buffer controlled_buffer_31
  assign controlled_buffer_1_out = I31 ? out_37 : 32'bz;  // Controlled_Buffer controlled_buffer_32
  REG32_LD reg32_ld_17 (.in_1(LD), .LD(I16), .out_4(out_22), .in_3(CLOCK));
  REG32_LD reg32_ld_18 (.in_1(LD), .LD(I17), .out_4(out_23), .in_3(CLOCK));
  REG32_LD reg32_ld_19 (.in_1(LD), .LD(I18), .out_4(out_24), .in_3(CLOCK));
  REG32_LD reg32_ld_20 (.in_1(LD), .LD(I19), .out_4(out_25), .in_3(CLOCK));
  REG32_LD reg32_ld_21 (.in_1(LD), .LD(I20), .out_4(out_26), .in_3(CLOCK));
  REG32_LD reg32_ld_22 (.in_1(LD), .LD(I21), .out_4(out_27), .in_3(CLOCK));
  REG32_LD reg32_ld_23 (.in_1(LD), .LD(I22), .out_4(out_28), .in_3(CLOCK));
  REG32_LD reg32_ld_24 (.in_1(LD), .LD(I23), .out_4(out_29), .in_3(CLOCK));
  assign not_1_out = ~Y;  // NOT_Gate not_1, 32 bits wide
  assign and_1_out = controlled_buffer_1_out & not_1_out;  // AND_Gate and_1, 32 bits wide
  assign or_1_out = controlled_buffer_1_out | Y;  // OR_Gate or_1, 32 bits wide
  Multiplexer #(.width(32)) multiplexer_1 (
    .in0(and_1_out), .in1(or_1_out), .out(multiplexer_1_out), .sel(SET_CLEAR));  // open: en
  REG32_LD reg32_ld_25 (.in_1(LD), .LD(I24), .out_4(out_30), .in_3(CLOCK));
  REG32_LD reg32_ld_26 (.in_1(LD), .LD(I25), .out_4(out_31), .in_3(CLOCK));
  REG32_LD reg32_ld_27 (.in_1(LD), .LD(I26), .out_4(out_32), .in_3(CLOCK));
  REG32_LD reg32_ld_28 (.in_1(LD), .LD(I27), .out_4(out_33), .in_3(CLOCK));
  REG32_LD reg32_ld_29 (.in_1(LD), .LD(I28), .out_4(out_34), .in_3(CLOCK));
  REG32_LD reg32_ld_30 (.in_1(LD), .LD(I29), .out_4(out_35), .in_3(CLOCK));
  REG32_LD reg32_ld_31 (.in_1(LD), .LD(I30), .out_4(out_36), .in_3(CLOCK));
  REG32_LD reg32_ld_32 (.in_1(LD), .LD(I31), .out_4(out_37), .in_3(CLOCK));
  Multiplexer #(.width(32)) multiplexer_2 (
    .in0(controlled_buffer_1_out), .in1(multiplexer_1_out), .out(LD), .sel(ENABLE));  // open: en
  Decoder #(.select(5)) decoder_2 (
    .out0(Y[0]), .out1(Y[1]), .out2(Y[2]), .out3(Y[3]), .out4(Y[4]), .out5(Y[5]), .out6(Y[6]), .out7(Y[7]),
    .out8(Y[8]), .out9(Y[9]), .out10(Y[10]), .out11(Y[11]), .out12(Y[12]), .out13(Y[13]), .out14(Y[14]),
    .out15(Y[15]), .out16(Y[16]), .out17(Y[17]), .out18(Y[18]), .out19(Y[19]), .out20(Y[20]), .out21(Y[21]),
    .out22(Y[22]), .out23(Y[23]), .out24(Y[24]), .out25(Y[25]), .out26(Y[26]), .out27(Y[27]), .out28(Y[28]),
    .out29(Y[29]), .out30(Y[30]), .out31(Y[31]), .sel(in_2));  // open: en

  // Other names for the same wires on the sheet: O0[31:0] = out_6; O1[31:0] = out_7; O2[31:0] = out_8;
  //   O3[31:0] = out_9; O4[31:0] = out_10; O5[31:0] = out_11; O6[31:0] = out_12; O7[31:0] = out_13; O8[31:0] = out_14;
  //   O9[31:0] = out_15; O10[31:0] = out_16; O11[31:0] = out_17; O12[31:0] = out_18; O13[31:0] = out_19;
  //   O14[31:0] = out_20; O15[31:0] = out_21; O16[31:0] = out_22; O17[31:0] = out_23; O18[31:0] = out_24;
  //   O19[31:0] = out_25; O20[31:0] = out_26; O21[31:0] = out_27; O22[31:0] = out_28; O23[31:0] = out_29;
  //   O24[31:0] = out_30; O25[31:0] = out_31; O26[31:0] = out_32; O27[31:0] = out_33; O28[31:0] = out_34;
  //   O29[31:0] = out_35; O30[31:0] = out_36; O31[31:0] = out_37; SET = SET_CLEAR; Ya[4:0] = in_2

  // Notes on the sheet:
  //   Y
  //   REG1028_LD
  //   Omogucava SET/CLEAR vrednosti 0..1027 preko X i Y
endmodule

module CONTR (
  input  in_1,
  input  in_2,
  input  in_3,
  input  in_4,
  output [4:0] out_5,
  output [4:0] out_6,
  output out_7
);

  wire clock_2_out, decX, decY, dole, incY, inpDesno, inpDole, inpGore, inpLevo, putLD;
  wire [1:0] priority_encoder_1_p3, reg2_ld_1_a1__0;

  Clock #(.highDuration(40), .lowDuration(40)) clock_1 (.out(out_7));
  Clock clock_2 (.out(clock_2_out));
  and and_1 (inpDesno, in_1, ~incY);  // AND_Gate
  and and_2 (inpLevo, in_2, ~decY);  // AND_Gate
  and and_3 (inpGore, in_3, ~dole);  // AND_Gate
  and and_4 (inpDole, in_4, ~decX);  // AND_Gate
  REG5_CL_INC_DEC_LD reg5_cl_inc_dec_ld_1 (
    .CLK(out_7), .INC(dole), .OUTPUT(out_5), .DEC(decX), .LD(1'b0));  // open: INPUT, CL
  REG5_CL_INC_DEC_LD reg5_cl_inc_dec_ld_2 (
    .CLK(out_7), .INC(incY), .OUTPUT(out_6), .DEC(decY), .LD(1'b0));  // open: INPUT, CL
  REG2_LD reg2_ld_1 (
    .LD(putLD), .CLK(clock_2_out), .I1__0(priority_encoder_1_p3), .A1__0(reg2_ld_1_a1__0));  // open: mr
  Decoder #(.select(2)) decoder_1 (
    .out0(decY), .out1(incY), .out2(decX), .out3(dole), .sel(reg2_ld_1_a1__0));  // open: en
  or or_1 (putLD, inpDesno, inpLevo, inpGore, inpDole);
  // Priority_Encoder #(.select(2)) priority_encoder_1: pin names not known; wires that end beside it: inpDesno, inpLevo, priority_encoder_1_p3, inpGore, inpDole

  // Other names for the same wires on the sheet: CLK = out_7; desno = decY; gore = decX; incX = dole; levo = incY;
  //   X[4:0] = out_5; Y[4:0] = out_6

  // Notes on the sheet:
  //   X
  //   Y
  //   PUTANJA
endmodule

module KONT_MEM (
  input  [4:0] in_1,
  input  [4:0] in_2,
  input  CLK,
  input  in_4,
  output [4:0] X,
  output [4:0] Y,
  output SET_CL,
  output Enable
);

  wire addrMEMX, and_2_out, and_3_out, and_5_out, BRX, decV, ldCNT, ldVAL, not_1_out, T0, T1, T3, VAL0, VAL1;
  wire [1:0] reg2_cl_inc_ld_1_a1__0;
  wire [3:0] controlled_buffer_1_out, datVAL, decVAL;
  wire [4:0] BR, datMEMX, datMEMY, multiplexer_1_out, multiplexer_2_out, multiplexer_3_out, N;

  Multiplexer #(.width(5)) multiplexer_1 (.in0(N), .in1(BR), .out(multiplexer_1_out), .sel(addrMEMX));  // open: en
  REG2_CL_INC_LD reg2_cl_inc_ld_1 (
    .I1__0({addrMEMX, 1'b0}), .LD(ldCNT), .CL(1'b0), .INC(not_1_out), .CLK(in_4),
    .A1__0(reg2_cl_inc_ld_1_a1__0));  // open: mr
  not not_1 (not_1_out, ldCNT);
  DC2_4 dc2_4_1 (.X1__0(reg2_cl_inc_ld_1_a1__0), .D0(T0), .D1(T1), .D2(addrMEMX), .D3(T3));  // open: En
  REG5_CL_INC reg5_cl_inc_1 (.CL(1'b0), .INC(SET_CL), .CLK(in_4), .A4__0(N));  // open: mr
  RAM #(.addrWidth(5), .dataWidth(5), .bus("separate")) ram_1 (
    .addr(multiplexer_1_out), .din(in_1), .data(datMEMX), .str(SET_CL), .clk(in_4), .ld(1'b1));  // open: sel, clr
  and and_1 (BRX, BR[0], BR[1], BR[2], BR[3], BR[4]);
  and and_2 (and_2_out, addrMEMX, ~BRX);  // AND_Gate
  or or_1 (ldCNT, and_2_out, and_3_out);
  Multiplexer #(.width(5)) multiplexer_2 (.in0(N), .in1(BR), .out(multiplexer_2_out), .sel(addrMEMX));  // open: en
  and and_3 (and_3_out, T0, ~CLK);  // AND_Gate
  REG5_CL_INC reg5_cl_inc_2 (.CL(SET_CL), .INC(addrMEMX), .CLK(in_4), .A4__0(BR));  // open: mr
  RAM #(.addrWidth(5), .dataWidth(5), .bus("separate")) ram_2 (
    .addr(multiplexer_2_out), .din(in_2), .data(datMEMY), .str(SET_CL), .clk(in_4), .ld(1'b1));  // open: sel, clr
  and and_4 (decV, addrMEMX, ~VAL0);  // AND_Gate
  and and_5 (and_5_out, addrMEMX, VAL1);
  or or_2 (ldVAL, SET_CL, decV);
  or or_3 (Enable, SET_CL, and_5_out);
  // Probe on multiplexer_3_out
  Multiplexer #(.width(5)) multiplexer_3 (.in0(N), .in1(BR), .out(multiplexer_3_out), .sel(addrMEMX));  // open: en
  Subtractor #(.width(4)) subtractor_1 (.a(datVAL), .b(4'b0001), .out(decVAL));  // open: bin, bout
  and and_6 (SET_CL, T0, CLK);
  assign controlled_buffer_1_out = SET_CL ? 4'b0111 : 4'bz;  // Controlled_Buffer controlled_buffer_1
  assign controlled_buffer_1_out = decV ? decVAL : 4'bz;  // Controlled_Buffer controlled_buffer_2
  RAM #(.addrWidth(5), .dataWidth(4), .bus("separate")) ram_3 (
    .addr(multiplexer_3_out), .din(controlled_buffer_1_out), .data(datVAL), .str(ldVAL), .clk(in_4), .ld(1'b1));  // open: sel, clr
  and and_7 (VAL1, datVAL[0], ~datVAL[1], ~datVAL[2], ~datVAL[3]);  // AND_Gate
  and and_8 (VAL0, ~datVAL[0], ~datVAL[1], ~datVAL[2], ~datVAL[3]);  // AND_Gate
  Multiplexer #(.width(5)) multiplexer_4 (.in0(datMEMX), .in1(in_1), .out(X), .sel(T0));  // open: en
  Multiplexer #(.width(5)) multiplexer_5 (.in0(datMEMY), .in1(in_2), .out(Y), .sel(T0));  // open: en

  // Other names for the same wires on the sheet: addrMEMY = addrMEMX; addrVAL = addrMEMX; CNT1 = addrMEMX;
  //   incBR = addrMEMX; T2 = addrMEMX; CAP = CLK; CLK_t = in_4; clBR = SET_CL; incN = SET_CL; ldMEMX = SET_CL;
  //   ldMEMY = SET_CL; ldV = SET_CL; X_t[4:0] = in_1; Y_t[4:0] = in_2

  // Notes on the sheet:
  //   X
  //   Y
  //   MEMX
  //   N
  //   MEMY
  //   BR
  //   VAL
endmodule

module REG32_LD (
  input  [31:0] in_1,
  input  LD,
  input  in_3,
  output [31:0] out_4
);

  Register #(.width(32)) register_1 (.D(in_1), .en(LD), .Q(out_4), .clk(in_3), .clr(1'b0));
endmodule

module REG5_CL_INC_DEC_LD (
  input  [4:0] INPUT,
  input  DEC,
  input  LD,
  input  CL,
  input  CLK,
  input  INC,
  output [4:0] OUTPUT
);

  wire not_1_out, or_1_out;
  wire [4:0] controlled_buffer_1_out, subtractor_1_out;

  not not_1 (not_1_out, DEC);
  assign controlled_buffer_1_out = not_1_out ? INPUT : 5'bz;  // Controlled_Buffer controlled_buffer_1
  assign controlled_buffer_1_out = DEC ? subtractor_1_out : 5'bz;  // Controlled_Buffer controlled_buffer_2
  REG5_CL_INC_LD reg5_cl_inc_ld_1 (
    .I4__0(controlled_buffer_1_out), .LD(or_1_out), .CL(CL), .INC(INC), .CLK(CLK), .A4__0(OUTPUT));  // open: mr
  Subtractor #(.width(5)) subtractor_1 (.a(OUTPUT), .b(5'b00001), .out(subtractor_1_out));  // open: bin, bout
  or or_1 (or_1_out, DEC, LD);
endmodule
